// Logisim project architecture_lab1_2.circ as structural Verilog: 1 circuit, main circuit main
module main (
);

  wire nand_1_out, nand_2_out, nand_3_out, nand_4_out, nand_5_out;

  nand nand_1 (nand_1_out, 1'b1, 1'b1);
  nand nand_2 (nand_2_out, 1'b0, 1'b0);
  nand nand_3 (nand_3_out, nand_1_out, 1'b0);
  nand nand_4 (nand_4_out, 1'b1, nand_2_out, nand_2_out);
  nand nand_5 (nand_5_out, nand_3_out, nand_4_out);
  // Probe on nand_5_out

  // Notes on the sheet:
  //   异或门
endmodule
