// Logisim project 2-bit_同步counter.circ as structural Verilog: 1 circuit, main circuit main
module main (
);

  wire and_1_out, and_2_out, clock_1_out, clock_2_out, d_ff_1_q, d_ff_1_qn, d_ff_2_q, j_k_ff_1_q, j_k_ff_2_q,
       nand_1_out, nand_2_out, or_1_out;

  or or_1 (or_1_out, and_1_out, and_2_out);
  Clock clock_1 (.out(clock_1_out));
  Clock clock_2 (.out(clock_2_out));
  and and_1 (and_1_out, nand_1_out, d_ff_2_q);
  and and_2 (and_2_out, nand_2_out, d_ff_1_q);
  LED led_1 (.in(j_k_ff_1_q));
  J_K_Flip_Flop #(.trigger("falling")) j_k_ff_1 (
    .J(j_k_ff_2_q), .clk(clock_2_out), .K(j_k_ff_2_q), .Q(j_k_ff_1_q));  // open: Qn, preset, en, reset
  D_Flip_Flop d_ff_1 (.clk(clock_1_out), .D(or_1_out), .Q(d_ff_1_q), .Qn(d_ff_1_qn));  // open: preset, en, reset
  nand nand_1 (nand_1_out, d_ff_1_q, d_ff_1_q);
  J_K_Flip_Flop #(.trigger("falling")) j_k_ff_2 (
    .J(1'b1), .clk(clock_2_out), .K(1'b1), .Q(j_k_ff_2_q));  // open: Qn, preset, en, reset
  LED led_2 (.in(d_ff_1_q));
  LED led_3 (.in(j_k_ff_2_q));
  nand nand_2 (nand_2_out, d_ff_2_q, d_ff_2_q);
  D_Flip_Flop d_ff_2 (.clk(clock_1_out), .D(d_ff_1_qn), .Q(d_ff_2_q));  // open: Qn, preset, en, reset
  LED led_4 (.in(d_ff_2_q));

  // Notes on the sheet:
  //   MSB
  //   LSB
endmodule
