// Logisim project 3-bit_异步counter_jk.circ as structural Verilog: 1 circuit, main circuit main
module main (
);

  wire clock_1_out, clock_2_out, clock_3_out, clock_4_out, clock_5_out, clock_6_out, d_ff_1_q, d_ff_1_qn,
       d_ff_2_q, d_ff_2_qn, d_ff_3_q, d_ff_3_qn, j_k_ff_1_q, j_k_ff_2_q, j_k_ff_3_q, j_k_ff_3_qn, j_k_ff_4_q,
       j_k_ff_5_q, j_k_ff_6_q, j_k_ff_6_qn, j_k_ff_7_q, j_k_ff_8_q, j_k_ff_9_qn, j_k_ff_10_q, j_k_ff_10_qn,
       j_k_ff_11_q, j_k_ff_11_qn, j_k_ff_12_q, t_ff_1_q, t_ff_2_q, t_ff_3_q;

  Clock clock_1 (.out(clock_1_out));
  Clock clock_2 (.out(clock_2_out));
  Clock clock_3 (.out(clock_3_out));
  Clock clock_4 (.out(clock_4_out));
  LED led_1 (.in(j_k_ff_1_q));
  J_K_Flip_Flop #(.trigger("falling")) j_k_ff_1 (
    .J(1'b1), .clk(clock_1_out), .K(1'b1), .Q(j_k_ff_1_q));  // open: Qn, preset, en, reset
  LED led_2 (.in(d_ff_1_q));
  D_Flip_Flop d_ff_1 (.clk(clock_3_out), .D(d_ff_1_qn), .Q(d_ff_1_q), .Qn(d_ff_1_qn));  // open: preset, en, reset
  LED led_3 (.in(j_k_ff_2_q));
  J_K_Flip_Flop j_k_ff_2 (.J(1'b1), .clk(clock_2_out), .K(1'b1), .Q(j_k_ff_2_q));  // open: Qn, preset, en, reset
  LED led_4 (.in(j_k_ff_3_qn));
  J_K_Flip_Flop #(.trigger("falling")) j_k_ff_3 (
    .J(1'b1), .clk(clock_4_out), .K(1'b1), .Q(j_k_ff_3_q), .Qn(j_k_ff_3_qn));  // open: preset, en, reset
  LED led_5 (.in(j_k_ff_4_q));
  J_K_Flip_Flop #(.trigger("falling")) j_k_ff_4 (
    .J(1'b1), .clk(j_k_ff_1_q), .K(1'b1), .Q(j_k_ff_4_q));  // open: Qn, preset, en, reset
  LED led_6 (.in(d_ff_2_q));
  D_Flip_Flop d_ff_2 (.clk(d_ff_1_qn), .D(d_ff_2_qn), .Q(d_ff_2_q), .Qn(d_ff_2_qn));  // open: preset, en, reset
  LED led_7 (.in(j_k_ff_5_q));
  J_K_Flip_Flop j_k_ff_5 (.J(1'b1), .clk(j_k_ff_2_q), .K(1'b1), .Q(j_k_ff_5_q));  // open: Qn, preset, en, reset
  LED led_8 (.in(j_k_ff_6_qn));
  J_K_Flip_Flop #(.trigger("falling")) j_k_ff_6 (
    .J(1'b1), .clk(j_k_ff_3_q), .K(1'b1), .Q(j_k_ff_6_q), .Qn(j_k_ff_6_qn));  // open: preset, en, reset
  LED led_9 (.in(j_k_ff_7_q));
  J_K_Flip_Flop #(.trigger("falling")) j_k_ff_7 (
    .J(1'b1), .clk(j_k_ff_4_q), .K(1'b1), .Q(j_k_ff_7_q));  // open: Qn, preset, en, reset
  D_Flip_Flop d_ff_3 (.clk(d_ff_2_qn), .D(d_ff_3_qn), .Q(d_ff_3_q), .Qn(d_ff_3_qn));  // open: preset, en, reset
  LED led_10 (.in(j_k_ff_8_q));
  J_K_Flip_Flop j_k_ff_8 (.J(1'b1), .clk(j_k_ff_5_q), .K(1'b1), .Q(j_k_ff_8_q));  // open: Qn, preset, en, reset
  LED led_11 (.in(d_ff_3_q));
  LED led_12 (.in(j_k_ff_9_qn));
  J_K_Flip_Flop #(.trigger("falling")) j_k_ff_9 (
    .J(1'b1), .clk(j_k_ff_6_q), .K(1'b1), .Qn(j_k_ff_9_qn));  // open: Q, preset, en, reset
  Clock clock_5 (.out(clock_5_out));
  Clock clock_6 (.out(clock_6_out));
  LED led_13 (.in(t_ff_1_q));
  T_Flip_Flop #(.trigger("falling")) t_ff_1 (.clk(clock_5_out), .T(1'b1), .Q(t_ff_1_q));  // open: Qn, preset, reset, en
  J_K_Flip_Flop #(.trigger("falling")) j_k_ff_10 (
    .J(1'b1), .clk(clock_6_out), .K(1'b1), .Q(j_k_ff_10_q), .Qn(j_k_ff_10_qn));  // open: preset, en, reset
  LED led_14 (.in(j_k_ff_10_q));
  LED led_15 (.in(t_ff_2_q));
  T_Flip_Flop #(.trigger("falling")) t_ff_2 (.clk(t_ff_1_q), .T(1'b1), .Q(t_ff_2_q));  // open: Qn, preset, reset, en
  LED led_16 (.in(j_k_ff_11_q));
  J_K_Flip_Flop #(.trigger("falling")) j_k_ff_11 (
    .J(1'b1), .clk(j_k_ff_10_qn), .K(1'b1), .Q(j_k_ff_11_q), .Qn(j_k_ff_11_qn));  // open: preset, en, reset
  LED led_17 (.in(t_ff_3_q));
  T_Flip_Flop #(.trigger("falling")) t_ff_3 (.clk(t_ff_2_q), .T(1'b1), .Q(t_ff_3_q));  // open: Qn, preset, reset, en
  LED led_18 (.in(j_k_ff_12_q));
  J_K_Flip_Flop #(.trigger("falling")) j_k_ff_12 (
    .J(1'b1), .clk(j_k_ff_11_qn), .K(1'b1), .Q(j_k_ff_12_q));  // open: Qn, preset, en, reset

  // Notes on the sheet:
  //   JK
  //   D FF
  //   JK
  //   up counter
  //   down counter
endmodule
