// Logisim project jk-ff-template.circ as structural Verilog: 1 circuit, main circuit main
module main (
);

  wire clock_1_out, multiplexer_1_out, multiplexer_2_out, multiplexer_3_out, multiplexer_4_out, nand_1_out,
       nand_2_out, undriven, undriven_2;

  Clock clock_1 (.out(clock_1_out));
  Multiplexer multiplexer_1 (.in0(undriven_2), .in1(1'b0), .out(multiplexer_1_out), .sel(1'b1));  // open: en
  Multiplexer multiplexer_2 (.in0(1'b1), .in1(1'b0), .out(multiplexer_2_out), .sel(1'b1));  // open: en
  Multiplexer multiplexer_3 (.in0(1'b0), .in1(1'b1), .out(multiplexer_3_out), .sel(1'b1));  // open: en
  Multiplexer multiplexer_4 (.in0(undriven), .in1(1'b1), .out(multiplexer_4_out), .sel(1'b1));  // open: en
  nand nand_1 (nand_1_out, multiplexer_1_out, multiplexer_2_out);
  nand nand_2 (nand_2_out, multiplexer_3_out, multiplexer_4_out);
  // NAND_Gate nand_3 is placed but not wired
  // NAND_Gate nand_4 is placed but not wired

  // Notes on the sheet:
  //   J
  //   Clock
  //   K
  //   Reset'
  //   Feedback X
  //   Feedback Y
endmodule
