// Logisim project lab3.circ as structural Verilog: 1 circuit, main circuit main
module main (
);

  wire clock_1_out, clock_2_out, clock_3_out, clock_4_out, clock_5_out, nand_1_out, nand_2_out, nand_3_out,
       nand_4_out, nand_5_out, nand_6_out, nand_7_out, nand_8_out, nand_9_out, nand_10_out, nand_11_out,
       nand_12_out, nand_13_out, nand_14_out, nand_15_out, nand_16_out, nand_17_out, nand_18_out,
       nand_19_out, nand_20_out, nand_21_out, nand_22_out, nand_23_out, nand_24_out, nand_25_out,
       nand_26_out, nand_27_out, nand_28_out, nand_29_out, nand_30_out, nand_31_out, nand_32_out,
       nand_33_out, nand_34_out, nand_35_out, nand_36_out, nand_37_out, nand_38_out, nand_39_out,
       nand_40_out, nand_41_out, nand_42_out, nand_43_out, nand_44_out, nand_45_out, nand_46_out,
       nand_47_out, nand_48_out, nand_49_out, nand_50_out, nand_51_out, nand_52_out, nand_53_out,
       nand_54_out, nand_55_out, nand_56_out, nand_57_out, nand_58_out, nand_59_out, nand_60_out,
       nand_61_out, nand_62_out, nand_63_out, nand_64_out, nand_65_out, nand_66_out, nand_67_out,
       nand_68_out, nand_69_out, nand_70_out;

  // Probe on nothing
  Clock clock_1 (.out(clock_1_out));
  Clock clock_2 (.out(clock_2_out));
  Clock clock_3 (.out(clock_3_out));
  nand nand_1 (nand_1_out, 1'b0, nand_2_out);
  nand nand_2 (nand_2_out, nand_1_out, 1'b1);
  nand nand_3 (nand_3_out, clock_2_out, clock_2_out);
  // Probe on nand_1_out
  // Probe on nand_2_out
  nand nand_4 (nand_4_out, 1'b0, 1'b0);
  nand nand_5 (nand_5_out, nand_4_out, 1'b0);
  nand nand_6 (nand_6_out, 1'b1, clock_1_out);
  nand nand_7 (nand_7_out, nand_6_out, clock_1_out);
  nand nand_8 (nand_8_out, 1'b0, clock_3_out);
  nand nand_9 (nand_9_out, nand_8_out, clock_3_out);
  nand nand_10 (nand_10_out, nand_41_out, clock_3_out);
  nand nand_11 (nand_11_out, nand_10_out, clock_3_out);
  nand nand_12 (nand_12_out, nand_43_out, clock_3_out);
  nand nand_13 (nand_13_out, nand_12_out, clock_3_out);
  nand nand_14 (nand_14_out, clock_3_out, clock_3_out);
  nand nand_15 (nand_15_out, clock_1_out, clock_1_out);
  nand nand_16 (nand_16_out, 1'b0, nand_3_out);
  nand nand_17 (nand_17_out, nand_16_out, nand_3_out);
  nand nand_18 (nand_18_out, nand_8_out, nand_19_out);
  nand nand_19 (nand_19_out, nand_18_out, nand_9_out);
  nand nand_20 (nand_20_out, nand_10_out, nand_21_out);
  nand nand_21 (nand_21_out, nand_20_out, nand_11_out);
  nand nand_22 (nand_22_out, clock_3_out, clock_3_out);
  nand nand_23 (nand_23_out, nand_12_out, nand_24_out);
  nand nand_24 (nand_24_out, nand_23_out, nand_13_out);
  nand nand_25 (nand_25_out, clock_3_out, clock_3_out);
  nand nand_26 (nand_26_out, nand_4_out, nand_27_out);
  nand nand_27 (nand_27_out, nand_26_out, nand_5_out);
  nand nand_28 (nand_28_out, nand_6_out, nand_29_out);
  nand nand_29 (nand_29_out, nand_28_out, nand_7_out);
  nand nand_30 (nand_30_out, nand_3_out, nand_3_out);
  // Probe on nand_26_out
  // Probe on nand_27_out
  nand nand_31 (nand_31_out, nand_16_out, nand_32_out);
  nand nand_32 (nand_32_out, nand_31_out, nand_17_out);
  nand nand_33 (nand_33_out, nand_18_out, nand_14_out);
  nand nand_34 (nand_34_out, nand_33_out, nand_14_out);
  nand nand_35 (nand_35_out, nand_20_out, nand_22_out);
  nand nand_36 (nand_36_out, nand_35_out, nand_22_out);
  nand nand_37 (nand_37_out, nand_23_out, nand_25_out);
  nand nand_38 (nand_38_out, nand_37_out, nand_25_out);
  nand nand_39 (nand_39_out, nand_28_out, nand_15_out);
  nand nand_40 (nand_40_out, nand_39_out, nand_15_out);
  nand nand_41 (nand_41_out, nand_33_out, nand_42_out);
  nand nand_42 (nand_42_out, nand_41_out, nand_34_out);
  nand nand_43 (nand_43_out, nand_35_out, nand_44_out);
  nand nand_44 (nand_44_out, nand_43_out, nand_36_out);
  nand nand_45 (nand_45_out, nand_37_out, nand_46_out);
  nand nand_46 (nand_46_out, nand_45_out, nand_38_out);
  nand nand_47 (nand_47_out, nand_31_out, nand_30_out);
  nand nand_48 (nand_48_out, nand_47_out, nand_30_out);
  // Probe on nand_41_out
  // Probe on nand_43_out
  nand nand_49 (nand_49_out, nand_39_out, nand_50_out);
  nand nand_50 (nand_50_out, nand_49_out, nand_40_out);
  // Probe on nand_45_out
  // Probe on nand_46_out
  // Probe on nand_49_out
  // Probe on nand_50_out
  nand nand_51 (nand_51_out, nand_47_out, nand_52_out);
  nand nand_52 (nand_52_out, nand_51_out, nand_48_out);
  // Probe on nand_51_out
  // Probe on nand_52_out
  Clock clock_4 (.out(clock_4_out));
  not nand_53 (nand_53_out, clock_4_out);  // NAND_Gate
  nand nand_54 (nand_54_out, nand_53_out, clock_4_out);
  nand nand_55 (nand_55_out, nand_53_out, nand_56_out);
  nand nand_56 (nand_56_out, nand_55_out, nand_54_out);
  nand nand_57 (nand_57_out, clock_4_out, clock_4_out);
  nand nand_58 (nand_58_out, nand_55_out, nand_57_out);
  nand nand_59 (nand_59_out, nand_58_out, nand_57_out);
  nand nand_60 (nand_60_out, nand_58_out, nand_61_out);
  nand nand_61 (nand_61_out, nand_60_out, nand_59_out);
  // Probe on nand_60_out
  // Probe on nand_61_out
  Clock clock_5 (.out(clock_5_out));
  nand nand_62 (nand_62_out, 1'b1, clock_5_out);
  nand nand_63 (nand_63_out, nand_62_out, clock_5_out);
  nand nand_64 (nand_64_out, clock_5_out, clock_5_out);
  nand nand_65 (nand_65_out, nand_62_out, nand_66_out);
  nand nand_66 (nand_66_out, nand_65_out, nand_63_out);
  nand nand_67 (nand_67_out, nand_65_out, nand_64_out);
  nand nand_68 (nand_68_out, nand_67_out, nand_64_out);
  nand nand_69 (nand_69_out, nand_67_out, nand_70_out);
  nand nand_70 (nand_70_out, nand_69_out, nand_68_out);
  // Probe on nand_69_out
  // Probe on nand_70_out

  // Notes on the sheet:
  //   S'
  //   R'
  //   D Latch
  //   D
  //   E
  //   D-type flip-flop 
  //   P
  //   E
  //   D-type flip-flop 
  //   P
  //   E
  //   P
  //   E
  //   SR Latch
  //   Level Sensivive
  //   Q'
  //   Q
  //   Falling-edge triggered ff
  //   Rising-edge triggered ff
  //   Shift register
  //   Q
  //   Q'
  //   Q
  //   Q'
  //   E
  //   P
  //   E
  //   Falling-edge triggered ff
endmodule
